// Logisim project Proj.circ as structural Verilog: 1 circuit, main circuit main
module main (
);

  wire _0, _1, _2, _3, _4, _5, _6, _7, _8, _9, button_1_out, not_1_out, or_5_out;
  wire [3:0] counter_1_q, or_1_out, ram_1_data, register_1_q, register_2_q;

  Button u__1 (.out(_1));
  Button u__4 (.out(_4));
  Button u__7 (.out(_7));
  Button u__2 (.out(_2));
  Button u__3 (.out(_3));
  Button u__6 (.out(_6));
  Button u__5 (.out(_5));
  Button u__9 (.out(_9));
  Button u__8 (.out(_8));
  Button u__0 (.out(_0));
  or or_1 (or_1_out[0], _1, _3, _5, _7, _9);
  or or_2 (or_1_out[1], _2, _3, _6, _7);
  or or_3 (or_1_out[2], _4, _5, _6, _7);
  or or_4 (or_1_out[3], _8, _9);
  Counter #(.width(4), .max('h6), .ongoal("load")) counter_1 (
    .Q(counter_1_q), .clk(or_5_out));  // open: load, D, count, carry, clr
  or or_5 (or_5_out, _0, or_1_out[0], or_1_out[1], or_1_out[2], or_1_out[3]);
  not not_1 (not_1_out, or_5_out);
  Register #(.width(4), .trigger("high")) register_1 (.D(or_1_out), .Q(register_1_q), .clk(or_5_out));  // open: en, clr
  Register #(.width(4), .trigger("high")) register_2 (
    .D(ram_1_data), .Q(register_2_q), .clk(not_1_out));  // open: en, clr
  RAM #(.addrWidth(4), .dataWidth(4), .bus("separate")) ram_1 (
    .addr(counter_1_q), .din(register_1_q), .data(ram_1_data), .clk(not_1_out), .clr(button_1_out));  // open: str, sel, ld
  Button button_1 (.out(button_1_out));
  Hex_Digit_Display hex_digit_display_1 (.value(register_2_q));  // open: dp
endmodule
